// Digital circuit HDC_Calc.dig as structural Verilog
module HDC_Calc (
  input  [7:0] R1,
  input  [7:0] R2,
  input  [7:0] R3,
  input  [7:0] R4,
  output [7:0] BUNDLE
);

  wire [7:0] BIND1, BIND2;

  assign BIND1 = R1 ^ R2;  // XOr xor_1, 8 bits wide
  assign BIND2 = R3 ^ R4;  // XOr xor_2, 8 bits wide
  assign BUNDLE = BIND1 & BIND2;  // And and_1, 8 bits wide
endmodule
